# Fritzing sketch Untitled Sketch (saved by Fritzing 0.9.10b)
breadboards: 1

parts:
  R1 = Resistor [tolerance=±5% power=0.25 resistance=10k package=THT]
  R2 = Resistor [tolerance=±5% power=0.25 resistance=2k package=THT]
  R3 = Resistor [tolerance=±5% power=0.25 resistance=3k package=THT]
  R4 = Resistor [tolerance=±5% power=0.25 resistance=5k package=THT]
  R5 = Resistor [tolerance=±5% power=0.25 resistance=20k package=THT]
  R6 = Resistor [tolerance=±5% power=0.25 resistance=5k package=THT]
  R7 = Resistor [tolerance=±5% power=0.25 resistance=7k package=THT]
  R8 = Resistor [tolerance=±5% power=0.25 resistance=8k package=THT]
  V1 = DC Power [voltage=15V]
  VM1 = Multimeter (DC Voltage)  # not connected

nets:
  N1: R1.Pin_0, R2.Pin_0, V1.V+
  N2: R1.Pin_1, R4.Pin_1, R5.Pin_0, R6.Pin_1
  N3: R2.Pin_1, R3.Pin_0
  N4: R3.Pin_1, R4.Pin_0
  N5: R5.Pin_1, R8.Pin_0
  N6: R6.Pin_0, R7.Pin_1
  N7: R7.Pin_0, R8.Pin_1
  GND: V1.V-
